# Fritzing sketch IPMI-esp32 (saved by Fritzing 0.9.5d)

parts:
  S1 = Pushbutton [part_number="RESET CONFIG" package=THT]
  D1 = Rectifier Diode [part_number=1N4001 package="300 mil [THT]"]
  D2 = Rectifier Diode [part_number=1N4001 package="300 mil [THT]"]
  J1 = ATX24 Pin Power Supply Connector [package=atx24_right_angle]
  R1 = Resistor [tolerance=±5% resistance=4.7k package=THT]
  U2 = ESP32-38PinWide [part_number=ESP32-38PinWide]
  R2 = Resistor [tolerance=±5% resistance=2.2k package=THT]
  JP1 = Header 5x2 [part_number="FRONT PANEL PC" package=2x5-ra]

nets:
  N1: S1.leg0, U2.GPIO35
  N2: D1.cathode, U2.GPIO4
  N3: D1.anode, JP1.6
  N4: D2.cathode, U2.GPIO2
  N5: D2.anode, JP1.7
  N6: J1.5V_STDBY, U2.VIN
  N7: R1.Pin_0, R2.Pin_1
  N8: R1.Pin_1, JP1.2
  N9: U2.GPIO11, JP1.8

custom parts:
  ESP32-38PinWide: Generic 38-Pin ESP32 with wide format (only access to one side of pins on a breadboard) based on Stephen Lilley's HiLetgo ESP-WROOM-32 ESP32 ESP-32S Development Board.
