# Fritzing sketch IPMI-wt32-eth01 (saved by Fritzing 0.9.5d)

parts:
  A1 = wt32-eth01
  S1 = Pushbutton [part_number="RESET CONFIG" package=THT]
  D1 = Rectifier Diode [part_number=1N4001 package="300 mil [THT]"]
  JP1 = Header 5x2 [part_number="FRONT PANEL PC" package=2x5-ra]
  D2 = Rectifier Diode [part_number=1N4001 package="300 mil [THT]"]
  J1 = ATX24 Pin Power Supply Connector [package=atx24_right_angle]
  R1 = Resistor [tolerance=±5% resistance=4.7k package=THT]
  R2 = Resistor [tolerance=±5% resistance=2.2k package=THT]

nets:
  N1: A1.Pin_2, A1.Pin_11, A1.Pin_14, S1.leg1, J1.GND
  N2: A1.Pin_12, J1.5V_STDBY
  N3: A1.Pin_15, D2.cathode
  N4: A1.Pin_16, D1.cathode
  N5: A1.Pin_17, S1.leg0
  N6: A1.Pin_21, R1.Pin_0, R2.Pin_1
  N7: D1.anode, JP1.6
  N8: JP1.2, R1.Pin_1
  N9: JP1.7, D2.anode
  N10: JP1.8, R2.Pin_0

custom parts:
  wt32-eth01: WT32-ETH01 is an embedded serial port to Ethernet module based on ESP32 series designed by Wireless-Tag.
